// Digital circuit FulllAdder1bit.dig as structural Verilog
module FulllAdder1bit (
  input  A,
  input  B,
  input  Cin,
  output Sum,
  output Cout
);

  wire and_1_out, and_2_out, xor_1_out;

  xor xor_1 (xor_1_out, A, B);
  and and_1 (and_1_out, A, B);
  and and_2 (and_2_out, Cin, xor_1_out);
  xor xor_2 (Sum, xor_1_out, Cin);
  or or_1 (Cout, and_1_out, and_2_out);
endmodule
