// Digital circuit number 6 .dig as structural Verilog
module number_6 (
  input  A1,
  input  A0,
  input  B1,
  input  B0,
  output P3,
  output P2,
  output P1,
  output P0,
  output C1
);

  wire and_2_out, and_3_out, and_4_out;

  and and_1 (P0, A0, B0);
  and and_2 (and_2_out, A1, B0);
  and and_3 (and_3_out, A0, B1);
  and and_4 (and_4_out, A1, B1);
  xor xor_1 (P2, and_4_out, C1);
  xor xor_2 (P1, and_2_out, and_3_out);
  and and_5 (C1, and_2_out, and_3_out);
  and and_6 (P3, and_4_out, C1);
endmodule
